# Fritzing sketch Esquema (saved by Fritzing 0.9.3b)
breadboards: 1

parts:
  Componente1 = Arduino Uno (Rev3)
  LED3 = LED - 5mm [color="White (6500K)" package="5 mm [THT]"]
  LED2 = LED - 5mm [color="White (6500K)" package="5 mm [THT]"]
  LED1 = LED - 5mm [color="White (6500K)" package="5 mm [THT]"]

nets:
  N1: Componente1.D2, LED1.cathode
  N2: Componente1.D3_PWM, LED2.cathode
  N3: Componente1.D4, LED3.cathode
  N4: Componente1.GND, LED3.anode, LED2.anode, LED1.anode
